// Logisim project Game.circ as structural Verilog: 1 circuit, main circuit main
module main (
);

  wire Change_shot_angle, Change_shot_force, Fire, Game_restart;
  wire [3:0] Lives_of__A, Lives_of__B, Player_turn, Selected_angle__ones, Selected_angle__tens,
       Selected_force, Winner;
  wire [15:0] main_1_p1, main_1_p2, main_1_p3, main_1_p4, main_1_p5, main_1_p6, main_1_p7, main_1_p8,
       main_1_p9, main_1_p10, main_1_p11, main_1_p12, main_1_p13, main_1_p14, main_1_p15, main_1_p16,
       main_1_p17, main_1_p18, main_1_p19, main_1_p20, main_1_p21, main_1_p22, main_1_p23, undriven,
       undriven_2, undriven_3, undriven_4, undriven_5, undriven_6, undriven_7, undriven_8, undriven_9;

  Button button_1 (.out(Game_restart));
  Hex_Digit_Display hex_digit_display_1 (.value(Lives_of__A));  // open: dp
  DotMatrix #(.matrixcols(32), .matrixrows(16)) dotmatrix_1 (
    .col0(undriven), .col1(undriven_2), .col2(undriven_3), .col3(undriven_4), .col4(undriven_5),
    .col5(undriven_6), .col6(undriven_7), .col7(undriven_8), .col8(undriven_9), .col9(main_1_p1),
    .col10(main_1_p2), .col11(main_1_p3), .col12(main_1_p4), .col13(main_1_p5), .col14(main_1_p6),
    .col15(main_1_p7), .col16(main_1_p8), .col17(main_1_p9), .col18(main_1_p10), .col19(main_1_p11),
    .col20(main_1_p12), .col21(main_1_p13), .col22(main_1_p14), .col23(main_1_p15), .col24(main_1_p16),
    .col25(main_1_p17), .col26(main_1_p18), .col27(main_1_p19), .col28(main_1_p20), .col29(main_1_p21),
    .col30(main_1_p22), .col31(main_1_p23));
  Hex_Digit_Display hex_digit_display_2 (.value(Winner));  // open: dp
  Hex_Digit_Display hex_digit_display_3 (.value(Player_turn));  // open: dp
  // SystemStrzelania_main main_1: pin names not known; wires that end beside it: main_1_p1, main_1_p2, main_1_p3, main_1_p4, main_1_p5, main_1_p6, main_1_p7, main_1_p8, main_1_p9, main_1_p10, main_1_p11, main_1_p12, main_1_p13, main_1_p14, main_1_p15, main_1_p16, main_1_p17, main_1_p18, main_1_p19, main_1_p20, main_1_p21, main_1_p22, main_1_p23, Game_restart, Change_shot_angle, Change_shot_force, Fire
  Hex_Digit_Display hex_digit_display_4 (.value(Lives_of__B));  // open: dp
  Hex_Digit_Display hex_digit_display_5 (.value(Selected_angle__tens));  // open: dp
  Hex_Digit_Display hex_digit_display_6 (.value(Selected_angle__ones));  // open: dp
  Button button_2 (.out(Change_shot_angle));
  Button button_3 (.out(Fire));
  Hex_Digit_Display hex_digit_display_7 (.value(Selected_force));  // open: dp
  Button button_4 (.out(Change_shot_force));

  // Notes on the sheet:
  //   Ctrl + K to enable ticking
  //   Recommended frequency: 8 Hz
endmodule
