// Logisim project ShootingSystem.circ as structural Verilog: 1 circuit, main circuit main
module main (
  input  Change_shot_angle,
  input  Change_shot_force,
  input  Take_the_shot,
  input  Game_reset,
  output [15:0] LED01,
  output [15:0] LED05,
  output [15:0] LED09,
  output [15:0] LED13,
  output [15:0] LED02,
  output [15:0] LED06,
  output [15:0] LED10,
  output [15:0] LED14,
  output [3:0] Selected_angle__tens,
  output [3:0] Selected_force__ones,
  output [3:0] Selected_angle__ones,
  output [15:0] LED03,
  output [15:0] LED07,
  output [15:0] LED11,
  output [15:0] LED15,
  output [3:0] Lives_of__A,
  output [3:0] Lives_of__B,
  output [3:0] Player_turn,
  output [3:0] Winner,
  output [15:0] LED04,
  output [15:0] LED08,
  output [15:0] LED12,
  output [15:0] LED16,
  output [15:0] LED17,
  output [15:0] LED21,
  output [15:0] LED25,
  output [15:0] LED29,
  output [15:0] LED18,
  output [15:0] LED22,
  output [15:0] LED26,
  output [15:0] LED30,
  output [15:0] LED19,
  output [15:0] LED23,
  output [15:0] LED27,
  output [15:0] LED31,
  output [15:0] LED20,
  output [15:0] LED24,
  output [15:0] LED28,
  output [15:0] LED32
);

  wire and_1_out, and_2_out, and_4_out, and_5_out, and_9_out, and_10_out, and_11_out, and_12_out, bCanTick,
       bCollision, bGameOngoing, bHitA, bHitB, bNextRound, bPlayer, clock_1_out, comparator_1_eq,
       comparator_2_eq, comparator_3_eq, comparator_4_eq, comparator_7_eq, comparator_8_eq, comparator_9_eq,
       comparator_10_eq, comparator_11_eq, comparator_12_eq, comparator_13_eq, comparator_14_eq,
       comparator_15_eq, comparator_16_eq, comparator_17_eq, comparator_19_eq, comparator_20_eq,
       Controlled_tick, counter_3_q, counter_4_q, not_1_out, not_2_out, not_3_out, not_4_out, not_5_out,
       not_6_out, not_7_out, not_8_out, not_9_out, not_10_out, or_2_out, or_3_out, or_4_out, or_5_out,
       or_6_out, or_7_out, or_8_out, or_9_out, or_10_out;
  wire [1:0] comparator_5_eq, comparator_21_eq, counter_1_q, counter_2_q, Elevation_of__A, Elevation_of__B;
  wire [2:0] Action_number, multiplexer_16_out, multiplexer_17_out, multiplexer_18_out, multiplexer_19_out,
       multiplexer_20_out, rom_5_data, rom_6_data, rom_7_data, rom_8_data, rom_9_data, rom_10_data,
       rom_11_data, rom_12_data, rom_13_data, rom_14_data, rom_15_data, rom_16_data, rom_17_data,
       rom_18_data, rom_19_data, rom_20_data, rom_21_data, rom_22_data, rom_23_data, rom_24_data,
       rom_25_data, rom_26_data, rom_27_data, rom_28_data, rom_29_data, Selected_angle, Selected_force;
  wire [3:0] CTRL_ELEV_1, CTRL_ELEV_2;
  wire [4:0] A__bullet_X_start__pos, adder_1_out, adder_2_out, adder_3_out, adder_4_out,
       B__bullet_X_start__pos, Bullet_X_position, counter_7_q, CTRL_DISPLACE, Current_bullet_X_start__pos,
       Current_X_offset, demultiplexer_1_out1, demultiplexer_1_out2, demultiplexer_1_out4,
       demultiplexer_4_out0, demultiplexer_4_out1, demultiplexer_5_out0, demultiplexer_5_out1,
       demultiplexer_5_out2, demultiplexer_5_out3, demultiplexer_5_out4, demultiplexer_6_out0,
       demultiplexer_6_out1, demultiplexer_6_out2, demultiplexer_6_out3, demultiplexer_6_out4,
       demultiplexer_7_out0, demultiplexer_7_out1, demultiplexer_7_out2, demultiplexer_7_out3,
       demultiplexer_7_out4, demultiplexer_8_out0, demultiplexer_8_out1, demultiplexer_8_out2,
       demultiplexer_8_out3, demultiplexer_8_out4, demultiplexer_9_out0, demultiplexer_9_out1,
       demultiplexer_9_out2, demultiplexer_9_out3, demultiplexer_9_out4, demultiplexer_10_out0,
       demultiplexer_10_out1, demultiplexer_10_out2, demultiplexer_10_out3, demultiplexer_10_out4,
       multiplexer_5_out, Right_column_of__B, subtractor_1_out, subtractor_2_out, subtractor_3_out,
       subtractor_4_out, subtractor_5_out;
  wire [15:0] A__bullet_Y_start__pos, A__bullet_Y_start__pos_t, B__bullet_Y_start__pos, Bullet_Y_position,
       Current_bullet_Y_start__pos, Current_Y_offset, demultiplexer_2_out2, demultiplexer_2_out3,
       demultiplexer_2_out4, demultiplexer_2_out5, demultiplexer_2_out6, demultiplexer_2_out7, DMX01, DMX02,
       DMX03, DMX04, DMX05, DMX06, DMX07, DMX08, DMX09, DMX10, DMX11, DMX12, DMX13, DMX14, DMX15, DMX16,
       DMX17, DMX18, DMX19, DMX20, DMX21, DMX22, DMX23, DMX24, DMX25, DMX26, DMX27, DMX28, DMX29, DMX30,
       DMX31, DMX32, multiplexer_4_out, multiplexer_8_out, or_1_out, shifter_1_out, shifter_2_out,
       shifter_3_out, shifter_4_out, shifter_5_out, shifter_6_out, TEREN01, TEREN02, TEREN03, TEREN04,
       TEREN05, TEREN06, TEREN07, TEREN08, TEREN09, TEREN10, TEREN11, TEREN12, TEREN13, TEREN14, TEREN15,
       TEREN16, TEREN17, TEREN18, TEREN19, TEREN20, TEREN21, TEREN22, TEREN23, TEREN24, TEREN25, TEREN26,
       TEREN27, TEREN28, TEREN29, TEREN30, TEREN31, TEREN32, Terrain_height_below_the_bullet;

  DotMatrix #(.matrixcols(32), .matrixrows(16)) dotmatrix_1 (
    .col0(LED01), .col1(LED02), .col2(LED03), .col3(LED04), .col4(LED05), .col5(LED06), .col6(LED07),
    .col7(LED08), .col8(LED09), .col9(LED10), .col10(LED11), .col11(LED12), .col12(LED13), .col13(LED14),
    .col14(LED15), .col15(LED16), .col16(LED17), .col17(LED18), .col18(LED19), .col19(LED20), .col20(LED21),
    .col21(LED22), .col22(LED23), .col23(LED24), .col24(LED25), .col25(LED26), .col26(LED27), .col27(LED28),
    .col28(LED29), .col29(LED30), .col30(LED31), .col31(LED32));
  Demultiplexer #(.select(3), .width(5), .enable("false")) demultiplexer_1 (
    .out1(demultiplexer_1_out1), .out2(demultiplexer_1_out2), .out4(demultiplexer_1_out4),
    .in(Current_X_offset), .sel(Action_number));  // open: out0, out3, out5, out6, out7
  Comparator #(.width(5)) comparator_1 (.a(Bullet_X_position), .b({5{1'b1}}), .eq(comparator_1_eq));  // open: gt, lt
  not not_1 (not_1_out, bPlayer);
  Comparator #(.width(5)) comparator_2 (.a(Bullet_X_position), .b({5{1'b0}}), .eq(comparator_2_eq));  // open: gt, lt
  Comparator #(.width(16)) comparator_3 (
    .a(Current_bullet_Y_start__pos), .b(Bullet_Y_position), .eq(comparator_3_eq));  // open: gt, lt
  Multiplexer #(.width(4), .enable("false")) multiplexer_1 (
    .in0(4'b0001), .in1(4'b0000), .out(CTRL_ELEV_1), .sel(comparator_4_eq));
  Comparator #(.width(16)) comparator_4 (.a(Bullet_Y_position), .b(16'h8000), .eq(comparator_4_eq));  // open: gt, lt
  Comparator #(.width(16)) comparator_5 (.a(Bullet_Y_position), .b(16'h4000), .eq(comparator_5_eq[0]));  // open: gt, lt
  Comparator #(.width(16)) comparator_6 (.a(Bullet_Y_position), .b(16'h8000), .eq(comparator_5_eq[1]));  // open: gt, lt
  assign or_1_out = Terrain_height_below_the_bullet | Bullet_Y_position;  // OR_Gate or_1, 16 bits wide
  and and_1 (and_1_out, comparator_1_eq, not_1_out);
  or or_2 (or_2_out, and_1_out, and_2_out);
  and and_2 (and_2_out, comparator_2_eq, bPlayer);
  Comparator #(.width(16)) comparator_7 (.a(Bullet_Y_position), .b({16{1'b0}}), .eq(comparator_7_eq));  // open: gt, lt
  Multiplexer #(.width(5), .enable("false")) multiplexer_2 (
    .in0(5'b00001), .in1({5{1'b0}}), .out(CTRL_DISPLACE), .sel(or_2_out));
  Comparator #(.width(16)) comparator_8 (.a(Bullet_Y_position), .b({16{1'b0}}), .eq(comparator_8_eq));  // open: gt, lt
  Multiplexer #(.select(2), .width(4), .enable("false")) multiplexer_3 (
    .in0(4'b0010), .in1(4'b0001), .in2(4'b0000), .out(CTRL_ELEV_2), .sel(comparator_5_eq));  // open: in3
  Comparator #(.width(16)) comparator_9 (
    .a(or_1_out), .b(Terrain_height_below_the_bullet), .eq(comparator_9_eq));  // open: gt, lt
  not not_2 (not_2_out, comparator_7_eq);
  not not_3 (not_3_out, Game_reset);
  Adder #(.width(5)) adder_1 (.a(demultiplexer_1_out1), .b(CTRL_DISPLACE), .out(adder_1_out));  // open: cin, cout
  Adder #(.width(5)) adder_2 (.a(demultiplexer_1_out2), .b(CTRL_DISPLACE), .out(adder_2_out));  // open: cin, cout
  Adder #(.width(5)) adder_3 (.a(demultiplexer_1_out4), .b(CTRL_DISPLACE), .out(adder_3_out));  // open: cin, cout
  Multiplexer #(.width(16), .enable("false")) multiplexer_4 (
    .in0(Bullet_Y_position), .in1(Current_bullet_Y_start__pos), .out(multiplexer_4_out), .sel(or_3_out));
  or or_3 (or_3_out, comparator_3_eq, comparator_8_eq);
  and and_3 (bCollision, comparator_9_eq, not_2_out, not_3_out);
  Multiplexer #(.select(3), .width(5), .enable("false")) multiplexer_5 (
    .in1(adder_1_out), .in2(adder_2_out), .in4(adder_3_out), .out(multiplexer_5_out), .sel(Action_number));  // open: in0, in3, in5, in6, in7
  Demultiplexer #(.select(3), .width(16), .enable("false")) demultiplexer_2 (
    .out2(demultiplexer_2_out2), .out3(demultiplexer_2_out3), .out4(demultiplexer_2_out4),
    .out5(demultiplexer_2_out5), .out6(demultiplexer_2_out6), .out7(demultiplexer_2_out7),
    .in(multiplexer_4_out), .sel(Action_number));  // open: out0, out1
  Hex_Digit_Display hex_digit_display_1 (.value(Selected_angle__tens));  // open: dp
  Hex_Digit_Display hex_digit_display_2 (.value(Player_turn));  // open: dp
  Register #(.width(5)) register_1 (
    .D(multiplexer_5_out), .Q(Current_X_offset), .clk(and_4_out), .clr(or_4_out));  // open: en
  or or_4 (or_4_out, Game_reset, bCollision);
  not not_4 (not_4_out, bCollision);
  Hex_Digit_Display hex_digit_display_3 (.value(Selected_angle__ones));  // open: dp
  and and_4 (and_4_out, Controlled_tick, not_4_out, not_5_out);
  Comparator #(.width(5)) comparator_10 (.a(Current_X_offset), .b({5{1'b1}}), .eq(comparator_10_eq));  // open: gt, lt
  Shifter #(.width(16)) shifter_1 (.in(demultiplexer_2_out2), .\dist (CTRL_ELEV_1), .out(shifter_1_out));
  Shifter #(.width(16)) shifter_2 (.in(demultiplexer_2_out3), .\dist (CTRL_ELEV_1), .out(shifter_2_out));
  Shifter #(.width(16), .shift("lr")) shifter_3 (.in(demultiplexer_2_out4), .\dist (4'b0001), .out(shifter_3_out));
  Shifter #(.width(16), .shift("lr")) shifter_4 (.in(demultiplexer_2_out5), .\dist (4'b0001), .out(shifter_4_out));
  Shifter #(.width(16)) shifter_5 (.in(demultiplexer_2_out6), .\dist (CTRL_ELEV_2), .out(shifter_5_out));
  Shifter #(.width(16), .shift("lr")) shifter_6 (.in(demultiplexer_2_out7), .\dist (4'b0010), .out(shifter_6_out));
  Hex_Digit_Display hex_digit_display_4 (.value({1'b0, Selected_force__ones[2:0]}));  // open: dp
  Hex_Digit_Display hex_digit_display_5 (.value(Winner));  // open: dp
  not not_5 (not_5_out, comparator_10_eq);
  Hex_Digit_Display hex_digit_display_6 (.value({2'b00, Lives_of__A[1:0]}));  // open: dp
  Multiplexer #(.width(5), .enable("false")) multiplexer_6 (
    .in0(A__bullet_X_start__pos), .in1(B__bullet_X_start__pos), .out(Current_bullet_X_start__pos),
    .sel(bPlayer));
  Multiplexer #(.width(16), .enable("false")) multiplexer_7 (
    .in0(A__bullet_Y_start__pos_t), .in1(B__bullet_Y_start__pos), .out(Current_bullet_Y_start__pos),
    .sel(bPlayer));
  Multiplexer #(.select(3), .width(16), .enable("false")) multiplexer_8 (
    .in2(shifter_1_out), .in3(shifter_2_out), .in4(shifter_3_out), .in5(shifter_4_out), .in6(shifter_5_out),
    .in7(shifter_6_out), .out(multiplexer_8_out), .sel(Action_number));  // open: in0, in1
  Demultiplexer #(.select(5), .width(16), .enable("false")) demultiplexer_3 (
    .out0(DMX01), .out1(DMX02), .out2(DMX03), .out3(DMX04), .out4(DMX05), .out5(DMX06), .out6(DMX07),
    .out7(DMX08), .out8(DMX09), .out9(DMX10), .out10(DMX11), .out11(DMX12), .out12(DMX13), .out13(DMX14),
    .out14(DMX15), .out15(DMX16), .out16(DMX17), .out17(DMX18), .out18(DMX19), .out19(DMX20), .out20(DMX21),
    .out21(DMX22), .out22(DMX23), .out23(DMX24), .out24(DMX25), .out25(DMX26), .out26(DMX27), .out27(DMX28),
    .out28(DMX29), .out29(DMX30), .out30(DMX31), .out31(DMX32), .in(Bullet_Y_position),
    .sel(Bullet_X_position));
  Hex_Digit_Display hex_digit_display_7 (.value({2'b00, Lives_of__B[1:0]}));  // open: dp
  not not_6 (not_6_out, bCollision);
  Demultiplexer #(.width(5), .enable("false")) demultiplexer_4 (
    .out0(demultiplexer_4_out0), .out1(demultiplexer_4_out1), .in(Current_bullet_X_start__pos), .sel(bPlayer));
  Register #(.width(16)) register_2 (
    .D(multiplexer_8_out), .Q(Current_Y_offset), .clk(and_5_out), .clr(or_5_out));  // open: en
  or or_5 (or_5_out, Game_reset, bCollision);
  and and_5 (and_5_out, Controlled_tick, not_6_out);
  Clock clock_1 (.out(clock_1_out));
  and and_6 (Controlled_tick, clock_1_out, bCanTick);
  Subtractor #(.width(5)) subtractor_1 (
    .a(Right_column_of__B), .b(5'b00001), .out(subtractor_1_out));  // open: bin, bout
  Subtractor #(.width(5)) subtractor_2 (
    .a(Right_column_of__B), .b(5'b00010), .out(subtractor_2_out));  // open: bin, bout
  Subtractor #(.width(5)) subtractor_3 (
    .a(A__bullet_X_start__pos), .b(5'b00001), .out(subtractor_3_out));  // open: bin, bout
  Subtractor #(.width(5)) subtractor_4 (
    .a(A__bullet_X_start__pos), .b(5'b00010), .out(subtractor_4_out));  // open: bin, bout
  Comparator #(.width(16)) comparator_11 (.a(Current_Y_offset), .b({16{1'b0}}), .eq(comparator_11_eq));  // open: gt, lt
  Comparator #(.width(5)) comparator_12 (
    .a(Bullet_X_position), .b(Right_column_of__B), .eq(comparator_12_eq));  // open: gt, lt
  Comparator #(.width(5)) comparator_13 (
    .a(Bullet_X_position), .b(subtractor_1_out), .eq(comparator_13_eq));  // open: gt, lt
  Comparator #(.width(5)) comparator_14 (
    .a(Bullet_X_position), .b(subtractor_2_out), .eq(comparator_14_eq));  // open: gt, lt
  Comparator #(.width(5)) comparator_15 (
    .a(Bullet_X_position), .b(A__bullet_X_start__pos), .eq(comparator_15_eq));  // open: gt, lt
  Comparator #(.width(5)) comparator_16 (
    .a(Bullet_X_position), .b(subtractor_3_out), .eq(comparator_16_eq));  // open: gt, lt
  Comparator #(.width(5)) comparator_17 (
    .a(Bullet_X_position), .b(subtractor_4_out), .eq(comparator_17_eq));  // open: gt, lt
  Adder #(.width(5)) adder_4 (.a(demultiplexer_4_out0), .b(Current_X_offset), .out(adder_4_out));  // open: cin, cout
  Subtractor #(.width(5)) subtractor_5 (
    .a(demultiplexer_4_out1), .b(Current_X_offset), .out(subtractor_5_out));  // open: bin, bout
  Multiplexer #(.width(16), .enable("false")) multiplexer_9 (
    .in0(Current_Y_offset), .in1(Current_bullet_Y_start__pos), .out(Bullet_Y_position), .sel(comparator_11_eq));
  Multiplexer #(.select(5), .width(16), .enable("false")) multiplexer_10 (
    .in0(TEREN01), .in1(TEREN02), .in2(TEREN03), .in3(TEREN04), .in4(TEREN05), .in5(TEREN06), .in6(TEREN07),
    .in7(TEREN08), .in8(TEREN09), .in9(TEREN10), .in10(TEREN11), .in11(TEREN12), .in12(TEREN13),
    .in13(TEREN14), .in14(TEREN15), .in15(TEREN16), .in16(TEREN17), .in17(TEREN18), .in18(TEREN19),
    .in19(TEREN20), .in20(TEREN21), .in21(TEREN22), .in22(TEREN23), .in23(TEREN24), .in24(TEREN25),
    .in25(TEREN26), .in26(TEREN27), .in27(TEREN28), .in28(TEREN29), .in29(TEREN30), .in30(TEREN31),
    .in31(TEREN32), .out(Terrain_height_below_the_bullet), .sel(Bullet_X_position));
  or or_6 (or_6_out, comparator_12_eq, comparator_13_eq, comparator_14_eq);
  or or_7 (or_7_out, comparator_15_eq, comparator_16_eq, comparator_17_eq);
  Multiplexer #(.width(5), .enable("false")) multiplexer_11 (
    .in0(adder_4_out), .in1(subtractor_5_out), .out(Bullet_X_position), .sel(bPlayer));
  and and_7 (bHitB, or_6_out, bCollision);
  and and_8 (bHitA, or_7_out, bCollision);
  Counter #(.width(2), .max('h3)) counter_1 (
    .Q(counter_1_q), .clk(bHitB), .clr(Game_reset));  // open: load, D, count, carry
  Counter #(.width(2), .max('h3)) counter_2 (
    .Q(counter_2_q), .clk(bHitA), .clr(Game_reset));  // open: load, D, count, carry
  Counter #(.width(1), .max('h1)) counter_3 (
    .Q(counter_3_q), .clk(bCollision), .clr(Game_reset));  // open: load, D, count, carry
  not not_7 (not_7_out, bCanTick);
  not not_8 (not_8_out, bCanTick);
  Multiplexer #(.width(4), .enable("false")) multiplexer_12 (
    .in0(4'b1010), .in1(4'b1011), .out(Player_turn), .sel(bPlayer));
  Comparator #(.width(1)) comparator_18 (.a(bPlayer), .b(1'b0), .eq(bNextRound));  // open: gt, lt
  TerrainGeneration_main main_1 (
    .K01(TEREN01), .K17(TEREN17), .K02(TEREN02), .K18(TEREN18), .K03(TEREN03), .K19(TEREN19), .K04(TEREN04),
    .K20(TEREN20), .K05(TEREN05), .K21(TEREN21), .K06(TEREN06), .K22(TEREN22), .K07(TEREN07), .K23(TEREN23),
    .K08(TEREN08), .K24(TEREN24), .K09(TEREN09), .K25(TEREN25), .K10(TEREN10), .K26(TEREN26), .K11(TEREN11),
    .K27(TEREN27), .K12(TEREN12), .K28(TEREN28), .K13(TEREN13), .K29(TEREN29), .K14(TEREN14), .K30(TEREN30),
    .K15(TEREN15), .K31(TEREN31), .K16(TEREN16), .K32(TEREN32), .Map_reset(Game_reset),
    .Wall_reset(or_9_out), .A__middle_column_position(A__bullet_X_start__pos),
    .B__middle_column_position(Right_column_of__B), .A_elevation(Elevation_of__A),
    .B_elevation(Elevation_of__B));
  Subtractor #(.width(2)) subtractor_6 (.a(2'b11), .b(counter_1_q), .out(Lives_of__B[1:0]));  // open: bin, bout
  Subtractor #(.width(2)) subtractor_7 (.a(2'b11), .b(counter_2_q), .out(Lives_of__A[1:0]));  // open: bin, bout
  Multiplexer #(.enable("false")) multiplexer_13 (.in0(1'b0), .in1(1'b1), .out(bPlayer), .sel(counter_3_q));
  Counter #(.width(1), .max('h1)) counter_4 (.Q(counter_4_q), .clk(or_8_out));  // open: load, D, count, carry, clr
  or or_8 (or_8_out, and_9_out, bCollision);
  and and_9 (and_9_out, Take_the_shot, bGameOngoing, not_9_out);
  Counter #(.width(3), .max('h7)) counter_5 (
    .Q(Selected_angle), .clk(and_10_out), .clr(comparator_19_eq));  // open: load, D, count, carry
  and and_10 (and_10_out, Change_shot_angle, not_7_out);
  Counter #(.width(3), .max('h7)) counter_6 (
    .Q(Selected_force), .clk(and_11_out), .clr(comparator_20_eq));  // open: load, D, count, carry
  and and_11 (and_11_out, Change_shot_force, not_8_out);
  Multiplexer #(.enable("false")) multiplexer_14 (.in0(1'b0), .in1(1'b1), .out(bCanTick), .sel(counter_4_q));
  not not_9 (not_9_out, bCanTick);
  Comparator #(.width(3)) comparator_19 (.a(Selected_angle), .b(3'b101), .eq(comparator_19_eq));  // open: gt, lt
  Comparator #(.width(3)) comparator_20 (.a(Selected_force), .b(3'b101), .eq(comparator_20_eq));  // open: gt, lt
  or or_9 (or_9_out, Game_reset, bNextRound);
  Multiplexer #(.select(2), .width(4), .enable("false")) multiplexer_15 (
    .in1(4'b1011), .in2(4'b1010), .in3(4'b1110), .out(Winner), .sel(comparator_21_eq));  // open: in0
  Comparator #(.width(2)) comparator_21 (.a(Lives_of__A[1:0]), .b(2'b00), .eq(comparator_21_eq[0]));  // open: gt, lt
  Comparator #(.width(2)) comparator_22 (.a(Lives_of__B[1:0]), .b(2'b00), .eq(comparator_21_eq[1]));  // open: gt, lt
  and and_12 (and_12_out, Controlled_tick, not_10_out);
  not not_10 (not_10_out, bCollision);
  Adder #(.width(3)) adder_5 (.a(Selected_force), .b(3'b001), .out(Selected_force__ones[2:0]));  // open: cin, cout
  Comparator #(.width(2)) comparator_23 (.a(comparator_21_eq), .b(2'b00), .eq(bGameOngoing));  // open: gt, lt
  Counter #(.width(5), .max('h1f)) counter_7 (
    .Q(counter_7_q), .clk(and_12_out), .clr(or_10_out));  // open: load, D, count, carry
  or or_10 (or_10_out, Game_reset, bCollision);
  ROM #(.addrWidth(3), .dataWidth(4)) rom_1 (.addr(Selected_angle), .data(Selected_angle__tens));  // open: sel
  ROM #(.addrWidth(3), .dataWidth(4)) rom_2 (.addr(Selected_angle), .data(Selected_angle__ones));  // open: sel
  Demultiplexer #(.select(3), .width(5), .enable("false")) demultiplexer_5 (
    .out0(demultiplexer_5_out0), .out1(demultiplexer_5_out1), .out2(demultiplexer_5_out2),
    .out3(demultiplexer_5_out3), .out4(demultiplexer_5_out4), .in(counter_7_q), .sel(Selected_angle));  // open: out5, out6, out7
  assign LED01 = DMX01 | TEREN01;  // OR_Gate or_11, 16 bits wide
  assign LED02 = DMX02 | TEREN02;  // OR_Gate or_12, 16 bits wide
  assign LED03 = DMX03 | TEREN03;  // OR_Gate or_13, 16 bits wide
  assign LED04 = DMX04 | TEREN04;  // OR_Gate or_14, 16 bits wide
  assign LED17 = DMX17 | TEREN17;  // OR_Gate or_15, 16 bits wide
  assign LED18 = DMX18 | TEREN18;  // OR_Gate or_16, 16 bits wide
  assign LED19 = DMX19 | TEREN19;  // OR_Gate or_17, 16 bits wide
  assign LED20 = DMX20 | TEREN20;  // OR_Gate or_18, 16 bits wide
  ROM #(.addrWidth(2), .dataWidth(16)) rom_3 (.addr(Elevation_of__A), .data(A__bullet_Y_start__pos));  // open: sel
  ROM #(.addrWidth(2), .dataWidth(16)) rom_4 (.addr(Elevation_of__B), .data(B__bullet_Y_start__pos));  // open: sel
  Subtractor #(.width(5)) subtractor_8 (
    .a(Right_column_of__B), .b(5'b00011), .out(B__bullet_X_start__pos));  // open: bin, bout
  Demultiplexer #(.select(3), .width(5), .enable("false")) demultiplexer_6 (
    .out0(demultiplexer_6_out0), .out1(demultiplexer_6_out1), .out2(demultiplexer_6_out2),
    .out3(demultiplexer_6_out3), .out4(demultiplexer_6_out4), .in(demultiplexer_5_out4), .sel(Selected_force));  // open: out5, out6, out7
  assign LED05 = DMX05 | TEREN05;  // OR_Gate or_19, 16 bits wide
  assign LED06 = DMX06 | TEREN06;  // OR_Gate or_20, 16 bits wide
  assign LED07 = DMX07 | TEREN07;  // OR_Gate or_21, 16 bits wide
  assign LED08 = DMX08 | TEREN08;  // OR_Gate or_22, 16 bits wide
  assign LED21 = DMX21 | TEREN21;  // OR_Gate or_23, 16 bits wide
  assign LED22 = DMX22 | TEREN22;  // OR_Gate or_24, 16 bits wide
  assign LED23 = DMX23 | TEREN23;  // OR_Gate or_25, 16 bits wide
  assign LED24 = DMX24 | TEREN24;  // OR_Gate or_26, 16 bits wide
  ROM #(.addrWidth(5), .dataWidth(3)) rom_5 (.addr(demultiplexer_6_out0), .data(rom_5_data));  // open: sel
  ROM #(.addrWidth(5), .dataWidth(3)) rom_6 (.addr(demultiplexer_6_out1), .data(rom_6_data));  // open: sel
  ROM #(.addrWidth(5), .dataWidth(3)) rom_7 (.addr(demultiplexer_6_out2), .data(rom_7_data));  // open: sel
  ROM #(.addrWidth(5), .dataWidth(3)) rom_8 (.addr(demultiplexer_6_out3), .data(rom_8_data));  // open: sel
  ROM #(.addrWidth(5), .dataWidth(3)) rom_9 (.addr(demultiplexer_6_out4), .data(rom_9_data));  // open: sel
  assign LED09 = DMX09 | TEREN09;  // OR_Gate or_27, 16 bits wide
  assign LED10 = DMX10 | TEREN10;  // OR_Gate or_28, 16 bits wide
  assign LED11 = DMX11 | TEREN11;  // OR_Gate or_29, 16 bits wide
  assign LED12 = DMX12 | TEREN12;  // OR_Gate or_30, 16 bits wide
  assign LED25 = DMX25 | TEREN25;  // OR_Gate or_31, 16 bits wide
  assign LED26 = DMX26 | TEREN26;  // OR_Gate or_32, 16 bits wide
  assign LED27 = DMX27 | TEREN27;  // OR_Gate or_33, 16 bits wide
  assign LED28 = DMX28 | TEREN28;  // OR_Gate or_34, 16 bits wide
  Multiplexer #(.select(3), .width(3), .enable("false")) multiplexer_16 (
    .in0(rom_5_data), .in1(rom_6_data), .in2(rom_7_data), .in3(rom_8_data), .in4(rom_9_data),
    .out(multiplexer_16_out), .sel(Selected_force));  // open: in5, in6, in7
  Demultiplexer #(.select(3), .width(5), .enable("false")) demultiplexer_7 (
    .out0(demultiplexer_7_out0), .out1(demultiplexer_7_out1), .out2(demultiplexer_7_out2),
    .out3(demultiplexer_7_out3), .out4(demultiplexer_7_out4), .in(demultiplexer_5_out3), .sel(Selected_force));  // open: out5, out6, out7
  assign LED13 = DMX13 | TEREN13;  // OR_Gate or_35, 16 bits wide
  assign LED14 = DMX14 | TEREN14;  // OR_Gate or_36, 16 bits wide
  assign LED15 = DMX15 | TEREN15;  // OR_Gate or_37, 16 bits wide
  assign LED16 = DMX16 | TEREN16;  // OR_Gate or_38, 16 bits wide
  assign LED29 = DMX29 | TEREN29;  // OR_Gate or_39, 16 bits wide
  assign LED30 = DMX30 | TEREN30;  // OR_Gate or_40, 16 bits wide
  assign LED31 = DMX31 | TEREN31;  // OR_Gate or_41, 16 bits wide
  assign LED32 = DMX32 | TEREN32;  // OR_Gate or_42, 16 bits wide
  ROM #(.addrWidth(5), .dataWidth(3)) rom_10 (.addr(demultiplexer_7_out0), .data(rom_10_data));  // open: sel
  ROM #(.addrWidth(5), .dataWidth(3)) rom_11 (.addr(demultiplexer_7_out1), .data(rom_11_data));  // open: sel
  ROM #(.addrWidth(5), .dataWidth(3)) rom_12 (.addr(demultiplexer_7_out2), .data(rom_12_data));  // open: sel
  ROM #(.addrWidth(5), .dataWidth(3)) rom_13 (.addr(demultiplexer_7_out3), .data(rom_13_data));  // open: sel
  ROM #(.addrWidth(5), .dataWidth(3)) rom_14 (.addr(demultiplexer_7_out4), .data(rom_14_data));  // open: sel
  Demultiplexer #(.select(3), .width(5), .enable("false")) demultiplexer_8 (
    .out0(demultiplexer_8_out0), .out1(demultiplexer_8_out1), .out2(demultiplexer_8_out2),
    .out3(demultiplexer_8_out3), .out4(demultiplexer_8_out4), .in(demultiplexer_5_out2), .sel(Selected_force));  // open: out5, out6, out7
  Multiplexer #(.select(3), .width(3), .enable("false")) multiplexer_17 (
    .in0(rom_10_data), .in1(rom_11_data), .in2(rom_12_data), .in3(rom_13_data), .in4(rom_14_data),
    .out(multiplexer_17_out), .sel(Selected_force));  // open: in5, in6, in7
  ROM #(.addrWidth(5), .dataWidth(3)) rom_15 (.addr(demultiplexer_8_out0), .data(rom_15_data));  // open: sel
  ROM #(.addrWidth(5), .dataWidth(3)) rom_16 (.addr(demultiplexer_8_out1), .data(rom_16_data));  // open: sel
  ROM #(.addrWidth(5), .dataWidth(3)) rom_17 (.addr(demultiplexer_8_out2), .data(rom_17_data));  // open: sel
  ROM #(.addrWidth(5), .dataWidth(3)) rom_18 (.addr(demultiplexer_8_out3), .data(rom_18_data));  // open: sel
  ROM #(.addrWidth(5), .dataWidth(3)) rom_19 (.addr(demultiplexer_8_out4), .data(rom_19_data));  // open: sel
  Multiplexer #(.select(3), .width(3), .enable("false")) multiplexer_18 (
    .in0(rom_15_data), .in1(rom_16_data), .in2(rom_17_data), .in3(rom_18_data), .in4(rom_19_data),
    .out(multiplexer_18_out), .sel(Selected_force));  // open: in5, in6, in7
  Demultiplexer #(.select(3), .width(5), .enable("false")) demultiplexer_9 (
    .out0(demultiplexer_9_out0), .out1(demultiplexer_9_out1), .out2(demultiplexer_9_out2),
    .out3(demultiplexer_9_out3), .out4(demultiplexer_9_out4), .in(demultiplexer_5_out1), .sel(Selected_force));  // open: out5, out6, out7
  ROM #(.addrWidth(5), .dataWidth(3)) rom_20 (.addr(demultiplexer_9_out0), .data(rom_20_data));  // open: sel
  ROM #(.addrWidth(5), .dataWidth(3)) rom_21 (.addr(demultiplexer_9_out1), .data(rom_21_data));  // open: sel
  ROM #(.addrWidth(5), .dataWidth(3)) rom_22 (.addr(demultiplexer_9_out2), .data(rom_22_data));  // open: sel
  ROM #(.addrWidth(5), .dataWidth(3)) rom_23 (.addr(demultiplexer_9_out3), .data(rom_23_data));  // open: sel
  ROM #(.addrWidth(5), .dataWidth(3)) rom_24 (.addr(demultiplexer_9_out4), .data(rom_24_data));  // open: sel
  Demultiplexer #(.select(3), .width(5), .enable("false")) demultiplexer_10 (
    .out0(demultiplexer_10_out0), .out1(demultiplexer_10_out1), .out2(demultiplexer_10_out2),
    .out3(demultiplexer_10_out3), .out4(demultiplexer_10_out4), .in(demultiplexer_5_out0),
    .sel(Selected_force));  // open: out5, out6, out7
  Multiplexer #(.select(3), .width(3), .enable("false")) multiplexer_19 (
    .in0(rom_20_data), .in1(rom_21_data), .in2(rom_22_data), .in3(rom_23_data), .in4(rom_24_data),
    .out(multiplexer_19_out), .sel(Selected_force));  // open: in5, in6, in7
  ROM #(.addrWidth(5), .dataWidth(3)) rom_25 (.addr(demultiplexer_10_out0), .data(rom_25_data));  // open: sel
  ROM #(.addrWidth(5), .dataWidth(3)) rom_26 (.addr(demultiplexer_10_out1), .data(rom_26_data));  // open: sel
  ROM #(.addrWidth(5), .dataWidth(3)) rom_27 (.addr(demultiplexer_10_out2), .data(rom_27_data));  // open: sel
  ROM #(.addrWidth(5), .dataWidth(3)) rom_28 (.addr(demultiplexer_10_out3), .data(rom_28_data));  // open: sel
  ROM #(.addrWidth(5), .dataWidth(3)) rom_29 (.addr(demultiplexer_10_out4), .data(rom_29_data));  // open: sel
  Multiplexer #(.select(3), .width(3), .enable("false")) multiplexer_20 (
    .in0(rom_25_data), .in1(rom_26_data), .in2(rom_27_data), .in3(rom_28_data), .in4(rom_29_data),
    .out(multiplexer_20_out), .sel(Selected_force));  // open: in5, in6, in7
  Multiplexer #(.select(3), .width(3), .enable("false")) multiplexer_21 (
    .in0(multiplexer_20_out), .in1(multiplexer_19_out), .in2(multiplexer_18_out), .in3(multiplexer_17_out),
    .in4(multiplexer_16_out), .out(Action_number), .sel(Selected_angle));  // open: in5, in6, in7

  assign Lives_of__A[3:2] = 2'b00;
  assign Lives_of__B[3:2] = 2'b00;
  assign Selected_force__ones[3] = 1'b0;

  // Other names for the same wires on the sheet: Fire = Take_the_shot; Lives_of_A__2_bit[1:0] = Lives_of__A[1:0];
  //   Lives_of_B__2_bit[1:0] = Lives_of__B[1:0]; Reset = Game_reset; Right_column_of__A[4:0] = A__bullet_X_start__pos;
  //   Shot_angle_selection = Change_shot_angle; Shot_force_selection = Change_shot_force

  // Notes on the sheet:
  //   CTRL_DISPLACE forbids the bullet from getting out of horizontal bounds
  //   CTRL_ELEV forbids the bullet from getting out of the upper bound
  //   Recommended frequency: 8 Hz
  //   Input
  //   This makes it so collision is not detected if the bullet is not yet spawned
  //   Collision detection
  //   Output
  //   Setting the starting position of the bullet
  //   CRUCIAL: The Y position of the bullet is a single, floating bit,
  //   Clock control -  thanks to this, the bullet moves only upon firing it
  //   This determines, whether the bullet should move left or right, based on the current active player
  //   Without this, the bullet is not displayed during the first frame of its animation
  //   while the X position is a true number representing the offset from the left LED border
  //   Player hit registration and life number control
  //   Displaying player turn and updating the wall every round
  //   Changing the active player after collision has been detected && stopping the clock
  //   0 -> Player 'A', 1 -> Player' B'
  //   Displaying and selecting the force and angle of each shot
  //   Displaying the winner
  //   0 - nothing
  //   1 - 1 to the side
  //   2 - 1 to the side and 1 upwards
  //   3 - 1 upwards
  //   5 - 1 downwards
  //   6 - 2 upwards
  //   7 - 2 downwards
  //   contents of rom_1 (hex, n*v repeats v):
  //   1 3 4 6 7
  //   contents of rom_2 (hex, n*v repeats v):
  //   5 0 5 0 5
  //   4 -  1 to the side and 1 downwards
  //   contents of rom_3 (hex, n*v repeats v):
  //   20 40 80 100
  //   contents of rom_4 (hex, n*v repeats v):
  //   20 40 80 100
  //   75 1
  //   75 2
  //   75 3
  //   75 4
  //   75 5
  //   Display
  //   contents of rom_5 (hex, n*v repeats v):
  //   2 2 3 2 3 2 1 4 5 4 5 4 4 19*5
  //   contents of rom_6 (hex, n*v repeats v):
  //   2 2 3 2 2 3 2 1 4 5 4 4 5 4 4 17*5
  //   contents of rom_7 (hex, n*v repeats v):
  //   2 2 3 2 3 2 2 2 1 4 4 4 5 4 5 4 4 15*5
  //   contents of rom_8 (hex, n*v repeats v):
  //   2 2 3 2 3 5*2 1 5*4 5 4 5 4 4 11*5
  //   contents of rom_9 (hex, n*v repeats v):
  //   2 2 3 2 3 2 2 3 4*2 1 1 4*4 5 4 4 5 4 5 4 4 6*5
  //   60 1
  //   60 2
  //   60 3
  //   60 4
  //   60 5
  //   contents of rom_10 (hex, n*v repeats v):
  //   2 2 3 2 2 1 4 4 5 4 22*5
  //   contents of rom_11 (hex, n*v repeats v):
  //   2 2 3 2 2 2 1 4 4 4 5 4 20*5
  //   contents of rom_12 (hex, n*v repeats v):
  //   2 2 3 5*2 1 5*4 5 4 16*5
  //   contents of rom_13 (hex, n*v repeats v):
  //   2 2 3 5*2 1 2 1 4 1 5*4 5 4 12*5
  //   contents of rom_14 (hex, n*v repeats v):
  //   2 2 3 6*2 1 2 1 2 4 1 4 1 6*4 5 4 7*5
  //   45 1
  //   45 2
  //   45 3
  //   45 4
  //   45 5
  //   Giving the bullet movement system adequate action based on the selected force and angle
  //   contents of rom_15 (hex, n*v repeats v):
  //   5*2 1 1 5*4 20*5
  //   contents of rom_16 (hex, n*v repeats v):
  //   5*2 1 2 4 1 5*4 18*5
  //   contents of rom_17 (hex, n*v repeats v):
  //   7*2 1 1 7*4 16*5
  //   contents of rom_18 (hex, n*v repeats v):
  //   7*2 1 2 4 1 7*4 14*5
  //   contents of rom_19 (hex, n*v repeats v):
  //   7*2 1 2 1 2 1 4 1 4 1 7*4 9*5
  //   30 1
  //   30 2
  //   30 3
  //   30 4
  //   30 5
  //   contents of rom_20 (hex, n*v repeats v):
  //   2 2 2 1 2 1 2 1 4 1 4 1 4 4 4 17*5
  //   contents of rom_21 (hex, n*v repeats v):
  //   4*2 1 2 1 2 4 1 4 1 4*4 16*5
  //   contents of rom_22 (hex, n*v repeats v):
  //   4*2 1 2 1 1 2 1 4 1 1 4 1 4*4 13*5
  //   contents of rom_23 (hex, n*v repeats v):
  //   5*2 1 2 1 2 1 1 4 1 4 1 6*4 11*5
  //   contents of rom_24 (hex, n*v repeats v):
  //   5*2 1 2 1 1 2 1 4 1 1 4 1 5*4 7 10*5
  //   15 1
  //   15 2
  //   15 3
  //   15 4
  //   15 5
  //   contents of rom_25 (hex, n*v repeats v):
  //   2 2 2 1 2 1 1 4 1 4 4 4 20*5
  //   contents of rom_26 (hex, n*v repeats v):
  //   2 2 2 1 2 1 1 1 4 1 4 4 4 19*5
  //   contents of rom_27 (hex, n*v repeats v):
  //   2 2 2 1 1 2 1 1 1 4 1 1 4 4 4 17*5
  //   contents of rom_28 (hex, n*v repeats v):
  //   2 2 2 1 1 2 1 2 1 4 1 4 1 1 4 4 4 15*5
  //   contents of rom_29 (hex, n*v repeats v):
  //   2 2 2 1 2 1 1 2 1 1 1 4 1 1 4 1 1 4 1 4 4 4 10*5
endmodule
