// Logisim project TerrainGeneration.circ as structural Verilog: 1 circuit, main circuit main
module main (
  input  Map_reset,
  input  Wall_reset,
  output [15:0] K01,
  output [15:0] K17,
  output [4:0] A__middle_column_position,
  output [15:0] K02,
  output [15:0] K18,
  output [15:0] K03,
  output [15:0] K19,
  output [15:0] K04,
  output [15:0] K20,
  output [15:0] K05,
  output [15:0] K21,
  output [15:0] K06,
  output [15:0] K22,
  output [4:0] B__middle_column_position,
  output [15:0] K07,
  output [15:0] K23,
  output [15:0] K08,
  output [15:0] K24,
  output [15:0] K09,
  output [15:0] K25,
  output [15:0] K10,
  output [15:0] K26,
  output [15:0] K11,
  output [15:0] K27,
  output [15:0] K12,
  output [15:0] K28,
  output [15:0] K13,
  output [15:0] K29,
  output [15:0] K14,
  output [15:0] K30,
  output [15:0] K15,
  output [15:0] K31,
  output [15:0] K16,
  output [15:0] K32,
  output [1:0] A_elevation,
  output [1:0] B_elevation
);

  wire New_round;
  wire [1:0] Drawn_A_pos, Drawn_B_pos, Drawn_wall_X_pos, random_23_out, random_24_out, random_25_out,
       random_26_out, random_27_out, random_28_out, random_33_out, random_34_out, random_35_out,
       random_36_out, random_37_out, random_38_out;
  wire [2:0] random_1_out, random_2_out, random_3_out, random_4_out, random_5_out, random_6_out,
       random_7_out, random_8_out, random_9_out, random_10_out, random_11_out, random_12_out, random_13_out,
       random_14_out, random_15_out, random_16_out, random_17_out, random_18_out, random_19_out,
       random_20_out, random_21_out;
  wire [15:0] A01, A02, A03, adder_3_out, adder_4_out, adder_5_out, adder_6_out, adder_7_out, adder_8_out,
       B01, B02, B03, rom_9_data, rom_10_data, rom_11_data, rom_12_data, rom_22_data, rom_23_data,
       rom_24_data, rom_25_data, rom_26_data, rom_27_data, rom_28_data, rom_29_data, rom_30_data,
       rom_31_data, rom_32_data, rom_33_data, rom_34_data, rom_35_data, shifter_1_out, shifter_2_out,
       shifter_3_out, shifter_4_out, shifter_5_out, shifter_6_out, Wall_shape;

  Random #(.width(3), .seed(18363)) random_1 (.clk(Map_reset), .out(random_1_out));  // open: next, clr
  Random #(.width(3), .seed(352)) random_2 (.clk(Map_reset), .out(random_2_out));  // open: next, clr
  Random #(.width(3), .seed(56262)) random_3 (.clk(Map_reset), .out(random_3_out));  // open: next, clr
  Random #(.width(3), .seed(74874)) random_4 (.clk(Map_reset), .out(random_4_out));  // open: next, clr
  Random #(.width(3), .seed(13677)) random_5 (.clk(Map_reset), .out(random_5_out));  // open: next, clr
  Random #(.width(3), .seed(1585)) random_6 (.clk(Map_reset), .out(random_6_out));  // open: next, clr
  Random #(.width(3), .seed(1585)) random_7 (.clk(Map_reset), .out(random_7_out));  // open: next, clr
  Random #(.width(3), .seed(1585)) random_8 (.clk(Map_reset), .out(random_8_out));  // open: next, clr
  Random #(.width(3), .seed(198932)) random_9 (.clk(New_round), .out(random_9_out));  // open: next, clr
  Random #(.width(3), .seed(1111166367)) random_10 (.clk(New_round), .out(random_10_out));  // open: next, clr
  Random #(.width(3), .seed(694492)) random_11 (.clk(New_round), .out(random_11_out));  // open: next, clr
  Random #(.width(3), .seed(189942)) random_12 (.clk(New_round), .out(random_12_out));  // open: next, clr
  ROM #(.addrWidth(3), .dataWidth(16)) rom_1 (.addr(random_1_out), .data(K01));  // open: sel
  ROM #(.addrWidth(3), .dataWidth(16)) rom_2 (.addr(random_2_out), .data(K09));  // open: sel
  ROM #(.addrWidth(3), .dataWidth(16)) rom_3 (.addr(random_3_out), .data(K11));  // open: sel
  ROM #(.addrWidth(3), .dataWidth(16)) rom_4 (.addr(random_4_out), .data(K13));  // open: sel
  ROM #(.addrWidth(3), .dataWidth(16)) rom_5 (.addr(random_5_out), .data(K19));  // open: sel
  ROM #(.addrWidth(3), .dataWidth(16)) rom_6 (.addr(random_6_out), .data(K21));  // open: sel
  ROM #(.addrWidth(3), .dataWidth(16)) rom_7 (.addr(random_7_out), .data(K23));  // open: sel
  ROM #(.addrWidth(3), .dataWidth(16)) rom_8 (.addr(random_8_out), .data(K31));  // open: sel
  Random #(.width(3), .seed(9300453)) random_13 (.clk(New_round), .out(random_13_out));  // open: next, clr
  Random #(.width(3), .seed(21536734)) random_14 (.clk(Map_reset), .out(random_14_out));  // open: next, clr
  Random #(.width(3), .seed(24)) random_15 (.clk(Map_reset), .out(random_15_out));  // open: next, clr
  Random #(.width(3), .seed(6421)) random_16 (.clk(Map_reset), .out(random_16_out));  // open: next, clr
  Random #(.width(3), .seed(884456)) random_17 (.clk(Map_reset), .out(random_17_out));  // open: next, clr
  Random #(.width(3), .seed(14845)) random_18 (.clk(Map_reset), .out(random_18_out));  // open: next, clr
  Random #(.width(3), .seed(16)) random_19 (.clk(Map_reset), .out(random_19_out));  // open: next, clr
  Random #(.width(3), .seed(16)) random_20 (.clk(Map_reset), .out(random_20_out));  // open: next, clr
  Random #(.width(3), .seed(16)) random_21 (.clk(Map_reset), .out(random_21_out));  // open: next, clr
  Random #(.width(2), .seed(2390252)) random_22 (.clk(New_round), .out(Drawn_wall_X_pos));  // open: next, clr
  ROM #(.addrWidth(3), .dataWidth(16)) rom_9 (.addr(random_9_out), .data(rom_9_data));  // open: sel
  ROM #(.addrWidth(3), .dataWidth(16)) rom_10 (.addr(random_10_out), .data(rom_10_data));  // open: sel
  ROM #(.addrWidth(3), .dataWidth(16)) rom_11 (.addr(random_11_out), .data(rom_11_data));  // open: sel
  ROM #(.addrWidth(3), .dataWidth(16)) rom_12 (.addr(random_12_out), .data(rom_12_data));  // open: sel
  ROM #(.addrWidth(3), .dataWidth(16)) rom_13 (.addr(random_13_out), .data(Wall_shape));  // open: sel
  ROM #(.addrWidth(3), .dataWidth(16)) rom_14 (.addr(random_14_out), .data(K02));  // open: sel
  ROM #(.addrWidth(3), .dataWidth(16)) rom_15 (.addr(random_15_out), .data(K10));  // open: sel
  ROM #(.addrWidth(3), .dataWidth(16)) rom_16 (.addr(random_16_out), .data(K12));  // open: sel
  ROM #(.addrWidth(3), .dataWidth(16)) rom_17 (.addr(random_17_out), .data(K14));  // open: sel
  ROM #(.addrWidth(3), .dataWidth(16)) rom_18 (.addr(random_18_out), .data(K20));  // open: sel
  ROM #(.addrWidth(3), .dataWidth(16)) rom_19 (.addr(random_19_out), .data(K22));  // open: sel
  ROM #(.addrWidth(3), .dataWidth(16)) rom_20 (.addr(random_20_out), .data(K24));  // open: sel
  ROM #(.addrWidth(3), .dataWidth(16)) rom_21 (.addr(random_21_out), .data(K32));  // open: sel
  Multiplexer #(.select(2), .width(16), .enable("false")) multiplexer_1 (
    .in0(Wall_shape), .in1(rom_9_data), .in2(rom_9_data), .in3(rom_9_data), .out(K15), .sel(Drawn_wall_X_pos));
  Multiplexer #(.select(2), .width(16), .enable("false")) multiplexer_2 (
    .in0(Wall_shape), .in1(Wall_shape), .in2(rom_10_data), .in3(Wall_shape), .out(K16), .sel(Drawn_wall_X_pos));
  Multiplexer #(.select(2), .width(16), .enable("false")) multiplexer_3 (
    .in0(rom_11_data), .in1(Wall_shape), .in2(Wall_shape), .in3(Wall_shape), .out(K17), .sel(Drawn_wall_X_pos));
  Multiplexer #(.select(2), .width(16), .enable("false")) multiplexer_4 (
    .in0(rom_12_data), .in1(rom_12_data), .in2(Wall_shape), .in3(rom_12_data), .out(K18),
    .sel(Drawn_wall_X_pos));
  DotMatrix #(.matrixcols(32), .matrixrows(16)) dotmatrix_1 (
    .col0(K01), .col1(K02), .col2(K03), .col3(K04), .col4(K05), .col5(K06), .col6(K07), .col7(K08),
    .col8(K09), .col9(K10), .col10(K11), .col11(K12), .col12(K13), .col13(K14), .col14(K15), .col15(K16),
    .col16(K17), .col17(K18), .col18(K19), .col19(K20), .col20(K21), .col21(K22), .col22(K23), .col23(K24),
    .col24(K25), .col25(K26), .col26(K27), .col27(K28), .col28(K29), .col29(K30), .col30(K31), .col31(K32));
  or or_1 (New_round, Map_reset, Wall_reset);
  Random #(.width(2), .seed(82365)) random_23 (.clk(Map_reset), .out(random_23_out));  // open: next, clr
  Random #(.width(2), .seed(236577)) random_24 (.clk(Map_reset), .out(random_24_out));  // open: next, clr
  Random #(.width(2), .seed(9222)) random_25 (.clk(Map_reset), .out(random_25_out));  // open: next, clr
  Random #(.width(2), .seed(88888)) random_26 (.clk(Map_reset), .out(random_26_out));  // open: next, clr
  Random #(.width(2), .seed(222)) random_27 (.clk(Map_reset), .out(random_27_out));  // open: next, clr
  Random #(.width(2), .seed(662812)) random_28 (.clk(Map_reset), .out(random_28_out));  // open: next, clr
  ROM #(.addrWidth(2), .dataWidth(16)) rom_22 (.addr(random_23_out), .data(rom_22_data));  // open: sel
  ROM #(.addrWidth(2), .dataWidth(16)) rom_23 (.addr(random_24_out), .data(rom_23_data));  // open: sel
  ROM #(.addrWidth(2), .dataWidth(16)) rom_24 (.addr(random_25_out), .data(rom_24_data));  // open: sel
  ROM #(.addrWidth(2), .dataWidth(16)) rom_25 (.addr(random_26_out), .data(rom_25_data));  // open: sel
  ROM #(.addrWidth(2), .dataWidth(16)) rom_26 (.addr(random_27_out), .data(rom_26_data));  // open: sel
  ROM #(.addrWidth(2), .dataWidth(16)) rom_27 (.addr(random_28_out), .data(rom_27_data));  // open: sel
  Multiplexer #(.select(2), .width(16), .enable("false")) multiplexer_5 (
    .in0(A01), .in1(rom_22_data), .in2(rom_22_data), .in3(rom_22_data), .out(K03), .sel(Drawn_A_pos));
  Random #(.width(2), .seed(78)) random_29 (.clk(Map_reset), .out(A_elevation));  // open: next, clr
  Random #(.width(2), .seed(9999)) random_30 (.clk(Map_reset), .out(B_elevation));  // open: next, clr
  Multiplexer #(.select(2), .width(16), .enable("false")) multiplexer_6 (
    .in0(A02), .in1(A01), .in2(rom_23_data), .in3(rom_23_data), .out(K04), .sel(Drawn_A_pos));
  Multiplexer #(.select(2), .width(16), .enable("false")) multiplexer_7 (
    .in0(A03), .in1(A02), .in2(A01), .in3(rom_24_data), .out(K05), .sel(Drawn_A_pos));
  Multiplexer #(.select(2), .width(16), .enable("false")) multiplexer_8 (
    .in0(rom_25_data), .in1(A03), .in2(A02), .in3(A01), .out(K06), .sel(Drawn_A_pos));
  Multiplexer #(.select(2), .width(16), .enable("false")) multiplexer_9 (
    .in0(rom_26_data), .in1(rom_26_data), .in2(A03), .in3(A02), .out(K07), .sel(Drawn_A_pos));
  Multiplexer #(.select(2), .width(16), .enable("false")) multiplexer_10 (
    .in0(rom_27_data), .in1(rom_27_data), .in2(rom_27_data), .in3(A03), .out(K08), .sel(Drawn_A_pos));
  Random #(.width(2), .seed(37893)) random_31 (.clk(Map_reset), .out(Drawn_A_pos));  // open: next, clr
  Random #(.width(2), .seed(378)) random_32 (.clk(Map_reset), .out(Drawn_B_pos));  // open: next, clr
  Shifter #(.width(16)) shifter_1 (.in(16'hf), .\dist ({2'b00, A_elevation}), .out(shifter_1_out));
  Shifter #(.width(16)) shifter_2 (.in(16'h14), .\dist ({2'b00, A_elevation}), .out(shifter_2_out));
  Shifter #(.width(16)) shifter_3 (.in(16'hf), .\dist ({2'b00, A_elevation}), .out(shifter_3_out));
  Shifter #(.width(16)) shifter_4 (.in(16'h1f), .\dist ({2'b00, B_elevation}), .out(shifter_4_out));
  Shifter #(.width(16)) shifter_5 (.in(16'h15), .\dist ({2'b00, B_elevation}), .out(shifter_5_out));
  Shifter #(.width(16)) shifter_6 (.in(16'ha), .\dist ({2'b00, B_elevation}), .out(shifter_6_out));
  Adder #(.width(5)) adder_1 (
    .a(5'b00100), .b({3'b000, Drawn_A_pos}), .out(A__middle_column_position));  // open: cin, cout
  Adder #(.width(5)) adder_2 (
    .a(5'b11010), .b({3'b000, Drawn_B_pos}), .out(B__middle_column_position));  // open: cin, cout
  ROM #(.addrWidth(2), .dataWidth(16)) rom_28 (.addr(A_elevation), .data(rom_28_data));  // open: sel
  ROM #(.addrWidth(2), .dataWidth(16)) rom_29 (.addr(B_elevation), .data(rom_29_data));  // open: sel
  Random #(.width(2), .seed(82365)) random_33 (.clk(Map_reset), .out(random_33_out));  // open: next, clr
  Random #(.width(2), .seed(236577)) random_34 (.clk(Map_reset), .out(random_34_out));  // open: next, clr
  Random #(.width(2), .seed(9222)) random_35 (.clk(Map_reset), .out(random_35_out));  // open: next, clr
  Random #(.width(2), .seed(88888)) random_36 (.clk(Map_reset), .out(random_36_out));  // open: next, clr
  Random #(.width(2), .seed(222)) random_37 (.clk(Map_reset), .out(random_37_out));  // open: next, clr
  Random #(.width(2), .seed(662812)) random_38 (.clk(Map_reset), .out(random_38_out));  // open: next, clr
  Adder #(.width(16)) adder_3 (.a(shifter_1_out), .b(rom_28_data), .out(adder_3_out));  // open: cin, cout
  Adder #(.width(16)) adder_4 (.a(shifter_2_out), .b(rom_28_data), .out(adder_4_out));  // open: cin, cout
  Adder #(.width(16)) adder_5 (.a(shifter_3_out), .b(rom_28_data), .out(adder_5_out));  // open: cin, cout
  Adder #(.width(16)) adder_6 (.a(shifter_4_out), .b(rom_29_data), .out(adder_6_out));  // open: cin, cout
  Adder #(.width(16)) adder_7 (.a(shifter_5_out), .b(rom_29_data), .out(adder_7_out));  // open: cin, cout
  Adder #(.width(16)) adder_8 (.a(shifter_6_out), .b(rom_29_data), .out(adder_8_out));  // open: cin, cout
  assign A01 = adder_3_out;  // Buffer buffer_1, 16 bits wide
  assign A02 = adder_4_out;  // Buffer buffer_2, 16 bits wide
  DotMatrix #(.matrixcols(3), .matrixrows(16)) dotmatrix_2 (.col0(adder_3_out), .col1(adder_4_out), .col2(adder_5_out));
  assign A03 = adder_5_out;  // Buffer buffer_3, 16 bits wide
  assign B01 = adder_6_out;  // Buffer buffer_4, 16 bits wide
  assign B02 = adder_7_out;  // Buffer buffer_5, 16 bits wide
  DotMatrix #(.matrixcols(3), .matrixrows(16)) dotmatrix_3 (.col0(adder_6_out), .col1(adder_7_out), .col2(adder_8_out));
  assign B03 = adder_8_out;  // Buffer buffer_6, 16 bits wide
  ROM #(.addrWidth(2), .dataWidth(16)) rom_30 (.addr(random_33_out), .data(rom_30_data));  // open: sel
  ROM #(.addrWidth(2), .dataWidth(16)) rom_31 (.addr(random_34_out), .data(rom_31_data));  // open: sel
  ROM #(.addrWidth(2), .dataWidth(16)) rom_32 (.addr(random_35_out), .data(rom_32_data));  // open: sel
  ROM #(.addrWidth(2), .dataWidth(16)) rom_33 (.addr(random_36_out), .data(rom_33_data));  // open: sel
  ROM #(.addrWidth(2), .dataWidth(16)) rom_34 (.addr(random_37_out), .data(rom_34_data));  // open: sel
  ROM #(.addrWidth(2), .dataWidth(16)) rom_35 (.addr(random_38_out), .data(rom_35_data));  // open: sel
  Multiplexer #(.select(2), .width(16), .enable("false")) multiplexer_11 (
    .in0(B01), .in1(rom_30_data), .in2(rom_30_data), .in3(rom_30_data), .out(K25), .sel(Drawn_B_pos));
  Multiplexer #(.select(2), .width(16), .enable("false")) multiplexer_12 (
    .in0(B02), .in1(B01), .in2(rom_31_data), .in3(rom_31_data), .out(K26), .sel(Drawn_B_pos));
  Multiplexer #(.select(2), .width(16), .enable("false")) multiplexer_13 (
    .in0(B03), .in1(B02), .in2(B01), .in3(rom_32_data), .out(K27), .sel(Drawn_B_pos));
  Multiplexer #(.select(2), .width(16), .enable("false")) multiplexer_14 (
    .in0(rom_33_data), .in1(B03), .in2(B02), .in3(B01), .out(K28), .sel(Drawn_B_pos));
  Multiplexer #(.select(2), .width(16), .enable("false")) multiplexer_15 (
    .in0(rom_34_data), .in1(rom_34_data), .in2(B03), .in3(B02), .out(K29), .sel(Drawn_B_pos));
  Multiplexer #(.select(2), .width(16), .enable("false")) multiplexer_16 (
    .in0(rom_35_data), .in1(rom_35_data), .in2(rom_35_data), .in3(B03), .out(K30), .sel(Drawn_B_pos));

  // Other names for the same wires on the sheet: Reroll = Map_reset

  // Notes on the sheet:
  //   contents of rom_1 (hex, n*v repeats v):
  //   1f f 7 3 1 3 7 f
  //   contents of rom_2 (hex, n*v repeats v):
  //   1f f 7 3 1 3 7 f
  //   contents of rom_3 (hex, n*v repeats v):
  //   1f f 7 3 1 3 7 f
  //   contents of rom_4 (hex, n*v repeats v):
  //   1f f 7 3 1 3 7 f
  //   contents of rom_5 (hex, n*v repeats v):
  //   1f f 7 3 1 3 7 f
  //   contents of rom_6 (hex, n*v repeats v):
  //   1f f 7 3 1 3 7 f
  //   contents of rom_7 (hex, n*v repeats v):
  //   1f f 7 3 1 3 7 f
  //   contents of rom_8 (hex, n*v repeats v):
  //   1f f 7 3 1 3 7 f
  //   Generates the wall in the middle
  //   Generates independent terrain
  //   contents of rom_9 (hex, n*v repeats v):
  //   1f f 7 3 1 3 7 f
  //   contents of rom_10 (hex, n*v repeats v):
  //   1f f 7 3 1 3 7 f
  //   contents of rom_11 (hex, n*v repeats v):
  //   1f f 7 3 1 3 7 f
  //   contents of rom_12 (hex, n*v repeats v):
  //   1f f 7 3 1 3 7 f
  //   contents of rom_13 (hex, n*v repeats v):
  //   fff 87ff c3ff e1ff e1ff c3ff 87ff c3ff
  //   contents of rom_14 (hex, n*v repeats v):
  //   1f f 7 3 1 3 7 f
  //   contents of rom_15 (hex, n*v repeats v):
  //   1f f 7 3 1 3 7 f
  //   contents of rom_16 (hex, n*v repeats v):
  //   1f f 7 3 1 3 7 f
  //   contents of rom_17 (hex, n*v repeats v):
  //   1f f 7 3 1 3 7 f
  //   contents of rom_18 (hex, n*v repeats v):
  //   1f f 7 3 1 3 7 f
  //   contents of rom_19 (hex, n*v repeats v):
  //   1f f 7 3 1 3 7 f
  //   contents of rom_20 (hex, n*v repeats v):
  //   1f f 7 3 1 3 7 f
  //   contents of rom_21 (hex, n*v repeats v):
  //   1f f 7 3 1 3 7 f
  //   Input
  //   Terrain output
  //   Generates player A
  //   contents of rom_22 (hex, n*v repeats v):
  //   f 7 3 1
  //   contents of rom_23 (hex, n*v repeats v):
  //   f 7 3 1
  //   contents of rom_24 (hex, n*v repeats v):
  //   f 7 3 1
  //   contents of rom_25 (hex, n*v repeats v):
  //   f 7 3 1
  //   contents of rom_26 (hex, n*v repeats v):
  //   f 7 3 1
  //   contents of rom_27 (hex, n*v repeats v):
  //   f 7 3 1
  //   Generating and outputing the X positions of the players
  //   Generates player elevation
  //   contents of rom_28 (hex, n*v repeats v):
  //   0 1 3 7
  //   contents of rom_29 (hex, n*v repeats v):
  //   0 1 3 7
  //   Generates player B
  //   'A' middle column possible positions: 4-7
  //   contents of rom_30 (hex, n*v repeats v):
  //   f 7 3 1
  //   contents of rom_31 (hex, n*v repeats v):
  //   f 7 3 1
  //   contents of rom_32 (hex, n*v repeats v):
  //   f 7 3 1
  //   contents of rom_33 (hex, n*v repeats v):
  //   f 7 3 1
  //   contents of rom_34 (hex, n*v repeats v):
  //   f 7 3 1
  //   contents of rom_35 (hex, n*v repeats v):
  //   f 7 3 1
  //   'B' middle column possible positions: 26-29
endmodule
